// Logisim project full_adder.circ as structural Verilog: 2 circuits, main circuit half_adder
module half_adder (
  input  A,
  input  B,
  output S,
  output C_out
);

  xor xor_1 (S, A, B);
  and and_1 (C_out, A, B);
endmodule

module main (
  input  A,
  input  B,
  input  C_in,
  output S,
  output C_out
);

  wire half_adder_1_c_out, half_adder_2_c_out, half_adder_2_s;

  half_adder half_adder_1 (.A(A), .B(half_adder_2_s), .S(S), .C_out(half_adder_1_c_out));
  half_adder half_adder_2 (.A(B), .B(C_in), .S(half_adder_2_s), .C_out(half_adder_2_c_out));
  or or_1 (C_out, half_adder_1_c_out, half_adder_2_c_out);
endmodule
